# Fritzing sketch sketch (saved by Fritzing 0.9.9b)
breadboards: 2

parts:
  Součástka1 = MAX3232
  A1 = ESP32 DevKitc V4
  IC1 = ULN2803A [package=THT]  # not connected
  IC2 = ULN2803A [package=THT]  # not connected
  IC3 = ULN2803A [package=THT]  # not connected

nets:
  N1: Součástka1.VCC, A1.Pin_19
  N2: Součástka1.RXD, A1.Pin_34
  N3: Součástka1.TXD, A1.Pin_35
  N4: Součástka1.GND, A1.Pin_14, A1.Pin_32, A1.Pin_38

custom parts:
  MAX3232: A random MAX3232 Breakout Board from AliExpress (RS232-TTL-Converter)
  ESP32 DevKitc V4: ESP32-DevKitC board with ESP32-WROOM-32 module. ESP32-DevKitC V4 is a small-sized ESP32-based development board produced by Espressif. Most of the pins on the ESP module are broken out to the pin headers on the board. The pins D0, D1, D2, D3, CMD and CLK are used internally for communication between ESP32 and SPI flash memory. They are grouped on both sides near the USB connector. Avoid using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
